// Logisim project ULA+Teclado.circ as structural Verilog: 1 circuit, main circuit main
// zera
module main (
  input  in_1,
  input  in_2,
  input  in_3,
  input  in_4,
  input  in_5,
  input  in_6,
  input  in_7,
  input  in_8,
  output [6:0] out_9,
  output out_10,
  output [6:0] out_11
);

  wire and_2_out, and_3_out, \botão_1 , clock_1_out, clock_2_out, comparator_1_eq, comparator_2_eq,
       comparator_3_eq, comparator_4_eq, not_1_out, not_2_out, not_3_out, or_1_out, or_2_out, register_1_q,
       register_2_q, verifica_oi;
  wire [1:0] counter_3_q;
  wire [2:0] counter_1_q, counter_2_q;
  wire [6:0] buffer_1_out, multiplexer_1_out, oi, rom_1_data, saidaRam2;

  Clock clock_1 (.out(clock_1_out));
  Keyboard keyboard_1 (.clk(\botão_1 ), .re(in_4), .clr(in_2), .avail(out_10), .data(out_11));
  and and_1 (\botão_1 , in_4, clock_1_out);
  Multiplexer #(.width(7), .enable("false")) multiplexer_1 (
    .in0(out_11), .in1(oi), .out(multiplexer_1_out), .sel(verifica_oi));
  assign buffer_1_out = out_11;  // Buffer buffer_1, 7 bits wide
  TTY tty_1 (.data(multiplexer_1_out), .clk(\botão_1 ), .we(\botão_1 ), .clr(in_3));
  not not_1 (not_1_out, in_4);
  Counter #(.width(3), .max('h3)) counter_1 (
    .load(in_6), .Q(counter_1_q), .clk(\botão_1 ), .clr(or_1_out));  // open: D, count, carry
  or or_1 (or_1_out, in_7, and_2_out);
  Counter #(.width(3), .max('h3)) counter_2 (
    .load(in_1), .Q(counter_2_q), .clk(\botão_1 ), .clr(not_1_out));  // open: D, count, carry
  RAM #(.addrWidth(3), .dataWidth(7), .bus("separate")) ram_1 (
    .addr(counter_2_q), .din(buffer_1_out), .data(out_9), .str(\botão_1 ), .clk(\botão_1 ), .ld(in_5),
    .clr(not_1_out));  // open: sel
  ROM #(.addrWidth(3), .dataWidth(7)) rom_1 (.addr(counter_1_q), .data(rom_1_data));  // open: sel
  Multiplexer #(.width(7), .enable("false")) multiplexer_2 (
    .in0({7{1'b0}}), .in1(rom_1_data), .out(oi), .sel(not_2_out));
  not not_2 (not_2_out, and_2_out);
  Register #(.width(1)) register_1 (.D(verifica_oi), .Q(register_1_q), .clk(clock_2_out), .clr(in_8));  // open: en
  Clock clock_2 (.out(clock_2_out));
  and and_2 (and_2_out, not_3_out, verifica_oi);
  not not_3 (not_3_out, register_1_q);
  Comparator #(.width(7)) comparator_1 (.a(out_9), .b(7'b0001010), .eq(comparator_1_eq));  // open: gt, lt
  Counter #(.width(2), .max('h3), .ongoal("stay")) counter_3 (
    .Q(counter_3_q), .clk(comparator_2_eq), .clr(in_7));  // open: load, D, count, carry
  Comparator #(.width(7)) comparator_2 (.a(saidaRam2), .b(rom_1_data), .eq(comparator_2_eq));  // open: gt, lt
  Comparator #(.width(7)) comparator_3 (.a(rom_1_data), .b({7{1'b0}}), .eq(comparator_3_eq));  // open: gt, lt
  Register #(.width(1)) register_2 (
    .D(comparator_1_eq), .Q(register_2_q), .clk(comparator_1_eq), .clr(in_7));  // open: en
  Comparator #(.width(2)) comparator_4 (.a(2'b11), .b(counter_3_q), .eq(comparator_4_eq));  // open: gt, lt
  Multiplexer #(.width(7), .enable("false")) multiplexer_3 (
    .in1(out_9), .out(saidaRam2), .sel(register_2_q));  // open: in0
  Register #(.width(1)) register_3 (
    .D(comparator_4_eq), .Q(verifica_oi), .clk(comparator_4_eq), .clr(or_2_out));  // open: en
  and and_3 (and_3_out, verifica_oi, comparator_3_eq);
  or or_2 (or_2_out, in_7, and_3_out);
  D_Flip_Flop d_ff_1 ();  // open: clk, D, Q, Qn, preset, en, reset

  // Other names for the same wires on the sheet: saida_RAM[6:0] = out_9; zera = in_7; zera_o_clock_oi = verifica_oi

  // Notes on the sheet:
  //   contents of rom_1 (hex, n*v repeats v):
  //   6f 69 a
  //   Zera os clocks
endmodule
